# Fritzing sketch RaspberryPi_Smagribot (saved by Fritzing 0.9.4)
breadboards: 2

parts:
  Raspberry_Pi_1 = Raspberry Pi 3 [part_number=RPI-3-V1.2]
  hc-sr1 = hc-sr04
  R1 = Resistor [tolerance=±10% resistance=330 package="0805 [SMD]"]
  R2 = Resistor [tolerance=±5% resistance=220 package="0805 [SMD]"]
  DHT1 = DHT22 Humidity and Temperature Sensor
  DS1 = DS18B20 1-Wire Temperature Sensor Probe Cable
  R3 = Resistor [tolerance=±10% resistance=4.7k package="0805 [SMD]"]
  R4 = Resistor [tolerance=±5% resistance=220 package="1206 [SMD]"]
  JP1 = Header 4 [package=jst-4-pth]
  ADC1 = MCP3008 [package=dil16]  # not connected
  JP2 = Header 4 [package=jst-4-pth]  # not connected
  J2 = JST-03JQ-BT [part_number=JST-JQ-BT package=THT]  # not connected
  J1 = JST-B3P-VH [part_number=JST-B3P-VH package=THT]  # not connected

nets:
  3V3: Raspberry_Pi_1.3v3, DS1.VDD, R3.Pin_0
  N1: Raspberry_Pi_1.GPIO4, DS1.DQ, R3.Pin_1
  N2: Raspberry_Pi_1.GPIO22, DHT1.DATA, R4.Pin_0
  N3: Raspberry_Pi_1.GPIO5, JP1.2
  N4: Raspberry_Pi_1.GPIO6, JP1.3
  N5: Raspberry_Pi_1.GPIO24, hc-sr1.Trig
  N6: Raspberry_Pi_1.GPIO23, R1.Pin_1, R2.Pin_1
  GND: Raspberry_Pi_1.GND, hc-sr1.GND, R2.Pin_0, DHT1.GND, DS1.GND, JP1.1
  5V: Raspberry_Pi_1.5V, hc-sr1.VCC, JP1.4
  N7: hc-sr1.Echo, R1.Pin_0
  N8: DHT1.VDD, R4.Pin_1
